// Logisim project processor.circ as structural Verilog: 5 circuits, main circuit main
module main (
  input  in_1,
  input  in_2,
  input  in_3
);

  wire ALU_en, and_1_out, and_2_out, and_3_out, and_4_out, and_5_out, CLK,
       control_signals_generator_1_stage_1, control_signals_generator_1_stage_2,
       control_signals_generator_1_stage_3, control_signals_generator_1_stage_4,
       control_signals_generator_1_stage_5, CU_PC_reset, first_bit, immediate_bit, IR_en, load, mem_en,
       not_1_out, or_2_out, PC_en, PC_reset, Ra_en, Rb_en, reg_en, reg_write_en, Ry_en, Rz_en, S1, S2, S_ALU;
  wire [1:0] op_select;
  wire [3:0] op_code;
  wire [4:0] ID_Ra, ID_Rb, ID_Rc;
  wire [7:0] adder_1_out, address, multiplexer_1_out, multiplexer_2_out, next_pc, PC, pc_increment_val;
  wire [31:0] alu_1_output, immediate_value, Instruction, IR, memory_data, multiplexer_3_out,
       multiplexer_4_out, multiplexer_5_out, RA, RB, register_file_1_ra, register_file_1_rb,
       register_update_value;
  wire [31:8] RZ;

  Clock clock_1 (.out(CLK));
  Multiplexer #(.width(8), .enable("false")) multiplexer_1 (
    .in0(adder_1_out), .in1(next_pc), .out(multiplexer_1_out), .sel(1'b0));
  Register u_PC (.D(multiplexer_1_out), .en(PC_en), .Q(PC), .clk(CLK), .clr(PC_reset));
  // Probe on address
  not not_1 (not_1_out, load);
  ROM #(.dataWidth(32)) rom_1 (.addr(PC), .data(Instruction));  // open: sel
  // Probe on memory_data
  RAM #(.dataWidth(32), .bus("separate")) ram_1 (
    .addr(address), .din(RB), .data(memory_data), .str(not_1_out), .sel(mem_en), .clk(CLK), .ld(load),
    .clr(in_3));
  // Probe on immediate_value
  Multiplexer #(.width(8), .enable("false")) multiplexer_2 (
    .in0(8'h1), .in1(pc_increment_val), .out(multiplexer_2_out), .sel(1'b0));
  // Probe on Instruction
  register_file register_file_1 (
    .clock(CLK), .ID_Ra(ID_Ra), .register_write_enable(reg_write_en), .ID_Rb(ID_Rb),
    .R_in(register_update_value), .clear_registers(in_1), .ID_Rc(ID_Rc), .RA(register_file_1_ra),
    .RB(register_file_1_rb));
  or or_1 (PC_reset, in_2, CU_PC_reset);
  Adder adder_1 (.a(PC), .b(multiplexer_2_out), .out(adder_1_out));  // open: cin, cout
  // Probe on alu_1_output
  // Probe on multiplexer_3_out
  Multiplexer #(.width(32)) multiplexer_3 (
    .in0(alu_1_output), .in1(immediate_value), .out(multiplexer_3_out), .sel(S_ALU), .en(ALU_en));
  and and_1 (and_1_out, reg_en, Rz_en);
  and and_2 (and_2_out, reg_en, Ra_en);
  and and_3 (and_3_out, reg_en, Rb_en);
  Register #(.width(32)) u_RA (.D(register_file_1_ra), .en(and_2_out), .Q(RA), .clk(CLK), .clr(in_1));
  Register #(.width(32)) u_RB (.D(register_file_1_rb), .en(and_3_out), .Q(RB), .clk(CLK), .clr(in_1));
  // Probe on {RZ, address}
  Register #(.width(32), .trigger("high")) u_RZ (
    .D(multiplexer_3_out), .en(and_1_out), .Q({RZ, address}), .clk(CLK), .clr(in_1));
  // Probe on PC
  // Probe on op_code
  and and_4 (and_4_out, reg_en, IR_en);
  LED _1 (.in(control_signals_generator_1_stage_1));
  not not_2 (reg_en, CU_PC_reset);
  // Probe on ID_Rc
  // Probe on immediate_value
  Register #(.width(32)) u_IR (.D(Instruction), .en(and_4_out), .Q(IR), .clk(CLK), .clr(in_1));
  LED _2 (.in(control_signals_generator_1_stage_2));
  LED _3 (.in(control_signals_generator_1_stage_3));
  LED _4 (.in(control_signals_generator_1_stage_4));
  Multiplexer #(.width(32), .enable("false")) multiplexer_4 (
    .in0(RB), .in1(immediate_value), .out(multiplexer_4_out), .sel(or_2_out));
  or or_2 (or_2_out, immediate_bit, S1);
  Multiplexer #(.width(32), .enable("false")) multiplexer_5 (
    .in0(memory_data), .in1({RZ, address}), .out(multiplexer_5_out), .sel(S2));
  // Probe on IR
  // Probe on ID_Ra
  LED _5 (.in(control_signals_generator_1_stage_5));
  control_signals_generator control_signals_generator_1 (
    .op_code(op_code), .PC_en(PC_en), .S1(S1), .S2(S2), .reg_write_enable(reg_write_en), .Clock(CLK),
    .Stage_1(control_signals_generator_1_stage_1), .Stage_2(control_signals_generator_1_stage_2),
    .Stage_3(control_signals_generator_1_stage_3), .Stage_4(control_signals_generator_1_stage_4),
    .Stage_5(control_signals_generator_1_stage_5), .IR_en(IR_en), .Ra_en(Ra_en), .Rb_en(Rb_en),
    .Rz_en(Rz_en), .Ry_en(Ry_en), .S_ALU(S_ALU), .ALU_en(ALU_en), .load(load), .mem_en(mem_en),
    .HLT(CU_PC_reset));
  and and_5 (and_5_out, reg_en, Ry_en);
  Instrucion_Splitter instrucion_splitter_1 (
    .Instruction(IR), .op_code(op_code), .ID_Rc(ID_Rc), .ID_Rb(ID_Rb), .ID_Ra(ID_Ra),
    .Immediate_Value(immediate_value), .op_select(op_select), .First_Bit(first_bit),
    .Immediate_bit(immediate_bit));
  // Probe on op_select
  Register #(.width(32)) RY (.D(multiplexer_5_out), .en(and_5_out), .Q(register_update_value), .clk(CLK), .clr(in_1));
  // Probe on ID_Rb
  // Probe on register_update_value
  ALU alu_1 (.Input_1(RA), .Input_2(multiplexer_4_out), .Opeartion_selector(op_select), .Output(alu_1_output));
  // Probe on RA
  // Probe on multiplexer_4_out
  // Probe on RA
  // Probe on RB
  // Probe on {RZ, address}
  // Probe on {RZ, address}

  // Other names for the same wires on the sheet: RZ[7:0] = address; clear = in_1; user_pc_reset = in_2

  // Notes on the sheet:
  //   User controls
  //   Instruction Memory (ROM)
  //   Used to store the instructions in sequential order
  //   Data Memory (RAM)
  //   Used to store the 32-bit data
  //   Program Counter Generator
  //   Selection lines to the MUX were fixed as they are constant for our Instruction Set Architecture 
  //   Since we can load instructions from a pre-written text file into ROM and test the circuit, I have used ROM intead of RAM 
  //   contents of rom_1 (hex, n*v repeats v):
  //   30800000 1040000 21880000 d1080001 10044001 210c0000 d1080002 10044002 210c0000 d1080004 10044003
  //   210c0000 d1080008 10044004 210c0000 d1080010 10044005 210c0000 d1080020 10044006 210c0000 d1080040
  //   10044007 210c0000 d1080080 10044008 40000000
  //   Register File
  //   5 - STAGE RISC PIPELINE ARCHITECTURE
  //   Stage:
  //   Control Signals Generator
  //   Generates control signals for all instructions at each stage
  //   Instruction-Splitter
  //   Values of various Registers and Signals
  //   Helpful during the Testing of the circuit
  //   Splits the 32-bit instruction into parts
  //   ALU
  //   Generating 8-bit address from 32-bit value
  //   The 32-bit value is having Zeros in the beginning (First 24 MSBs)
endmodule

module register_file (
  input  clock,
  input  [4:0] ID_Ra,
  input  register_write_enable,
  input  [4:0] ID_Rb,
  input  [31:0] R_in,
  input  clear_registers,
  input  [4:0] ID_Rc,
  output [31:0] RA,
  output [31:0] RB
);

  wire R0_en, R1_en, R2_en, R3_en, R4_en, R5_en, R6_en, R7_en, R8_en, R9_en, R10_en, R11_en, R12_en, R13_en,
       R14_en, R15_en, R16_en, R17_en, R18_en, R19_en, R20_en, R21_en, R22_en, R23_en, R24_en, R25_en,
       R26_en, R27_en, R28_en, R29_en, R30_en, R31_en;
  wire [31:0] R0_out, R1_out, R2_out, R3_out, R4_out, R5_out, R6_out, R7_out, R8_out, R9_out, R10_out,
       R11_out, R12_out, R13_out, R14_out, R15_out, R16_out, R17_out, R18_out, R19_out, R20_out, R21_out,
       R22_out, R23_out, R24_out, R25_out, R26_out, R27_out, R28_out, R29_out, R30_out, R31_out;

  Register #(.width(32)) register_1 (.D(R_in), .en(R0_en), .Q(R0_out), .clk(clock), .clr(clear_registers));
  Register #(.width(32)) register_2 (.D(R_in), .en(R4_en), .Q(R4_out), .clk(clock), .clr(clear_registers));
  Register #(.width(32)) register_3 (.D(R_in), .en(R8_en), .Q(R8_out), .clk(clock), .clr(clear_registers));
  Register #(.width(32)) register_4 (.D(R_in), .en(R12_en), .Q(R12_out), .clk(clock), .clr(clear_registers));
  Register #(.width(32)) register_5 (.D(R_in), .en(R16_en), .Q(R16_out), .clk(clock), .clr(clear_registers));
  Register #(.width(32)) register_6 (.D(R_in), .en(R20_en), .Q(R20_out), .clk(clock), .clr(clear_registers));
  Register #(.width(32)) register_7 (.D(R_in), .en(R24_en), .Q(R24_out), .clk(clock), .clr(clear_registers));
  Register #(.width(32)) register_8 (.D(R_in), .en(R28_en), .Q(R28_out), .clk(clock), .clr(clear_registers));
  Register #(.width(32)) register_9 (.D(R_in), .en(R1_en), .Q(R1_out), .clk(clock), .clr(clear_registers));
  Register #(.width(32)) register_10 (.D(R_in), .en(R5_en), .Q(R5_out), .clk(clock), .clr(clear_registers));
  Register #(.width(32)) register_11 (.D(R_in), .en(R9_en), .Q(R9_out), .clk(clock), .clr(clear_registers));
  Register #(.width(32)) register_12 (.D(R_in), .en(R13_en), .Q(R13_out), .clk(clock), .clr(clear_registers));
  Register #(.width(32)) register_13 (.D(R_in), .en(R17_en), .Q(R17_out), .clk(clock), .clr(clear_registers));
  Register #(.width(32)) register_14 (.D(R_in), .en(R21_en), .Q(R21_out), .clk(clock), .clr(clear_registers));
  Register #(.width(32)) register_15 (.D(R_in), .en(R25_en), .Q(R25_out), .clk(clock), .clr(clear_registers));
  Register #(.width(32)) register_16 (.D(R_in), .en(R29_en), .Q(R29_out), .clk(clock), .clr(clear_registers));
  Register #(.width(32)) register_17 (.D(R_in), .en(R2_en), .Q(R2_out), .clk(clock), .clr(clear_registers));
  Register #(.width(32)) register_18 (.D(R_in), .en(R6_en), .Q(R6_out), .clk(clock), .clr(clear_registers));
  Register #(.width(32)) register_19 (.D(R_in), .en(R10_en), .Q(R10_out), .clk(clock), .clr(clear_registers));
  Register #(.width(32)) register_20 (.D(R_in), .en(R14_en), .Q(R14_out), .clk(clock), .clr(clear_registers));
  Register #(.width(32)) register_21 (.D(R_in), .en(R18_en), .Q(R18_out), .clk(clock), .clr(clear_registers));
  Register #(.width(32)) register_22 (.D(R_in), .en(R22_en), .Q(R22_out), .clk(clock), .clr(clear_registers));
  Register #(.width(32)) register_23 (.D(R_in), .en(R26_en), .Q(R26_out), .clk(clock), .clr(clear_registers));
  Register #(.width(32)) register_24 (.D(R_in), .en(R30_en), .Q(R30_out), .clk(clock), .clr(clear_registers));
  Register #(.width(32)) register_25 (.D(R_in), .en(R3_en), .Q(R3_out), .clk(clock), .clr(clear_registers));
  Register #(.width(32)) register_26 (.D(R_in), .en(R7_en), .Q(R7_out), .clk(clock), .clr(clear_registers));
  Register #(.width(32)) register_27 (.D(R_in), .en(R11_en), .Q(R11_out), .clk(clock), .clr(clear_registers));
  Register #(.width(32)) register_28 (.D(R_in), .en(R15_en), .Q(R15_out), .clk(clock), .clr(clear_registers));
  Register #(.width(32)) register_29 (.D(R_in), .en(R19_en), .Q(R19_out), .clk(clock), .clr(clear_registers));
  Register #(.width(32)) register_30 (.D(R_in), .en(R23_en), .Q(R23_out), .clk(clock), .clr(clear_registers));
  Register #(.width(32)) register_31 (.D(R_in), .en(R27_en), .Q(R27_out), .clk(clock), .clr(clear_registers));
  Register #(.width(32)) register_32 (.D(R_in), .en(R31_en), .Q(R31_out), .clk(clock), .clr(clear_registers));
  // Probe on R0_out
  // Probe on R1_out
  // Probe on R2_out
  // Probe on R3_out
  // Probe on R4_out
  // Probe on R5_out
  // Probe on R6_out
  // Probe on R7_out
  // Probe on R8_out
  // Probe on R9_out
  // Probe on R10_out
  // Probe on R11_out
  // Probe on R12_out
  // Probe on R13_out
  // Probe on R14_out
  // Probe on R15_out
  Multiplexer #(.select(5), .width(32), .enable("false")) multiplexer_1 (
    .in0(R0_out), .in1(R1_out), .in2(R2_out), .in3(R3_out), .in4(R4_out), .in5(R5_out), .in6(R6_out),
    .in7(R7_out), .in8(R8_out), .in9(R9_out), .in10(R10_out), .in11(R11_out), .in12(R12_out), .in13(R13_out),
    .in14(R14_out), .in15(R15_out), .in16(R16_out), .in17(R17_out), .in18(R18_out), .in19(R19_out),
    .in20(R20_out), .in21(R21_out), .in22(R22_out), .in23(R23_out), .in24(R24_out), .in25(R25_out),
    .in26(R26_out), .in27(R27_out), .in28(R28_out), .in29(R29_out), .in30(R30_out), .in31(R31_out), .out(RA),
    .sel(ID_Ra));
  Demultiplexer #(.select(5), .enable("false")) demultiplexer_1 (
    .out0(R0_en), .out1(R1_en), .out2(R2_en), .out3(R3_en), .out4(R4_en), .out5(R5_en), .out6(R6_en),
    .out7(R7_en), .out8(R8_en), .out9(R9_en), .out10(R10_en), .out11(R11_en), .out12(R12_en), .out13(R13_en),
    .out14(R14_en), .out15(R15_en), .out16(R16_en), .out17(R17_en), .out18(R18_en), .out19(R19_en),
    .out20(R20_en), .out21(R21_en), .out22(R22_en), .out23(R23_en), .out24(R24_en), .out25(R25_en),
    .out26(R26_en), .out27(R27_en), .out28(R28_en), .out29(R29_en), .out30(R30_en), .out31(R31_en),
    .in(register_write_enable), .sel(ID_Rc));
  // Probe on R16_out
  // Probe on R17_out
  // Probe on R18_out
  // Probe on R19_out
  // Probe on R20_out
  // Probe on R21_out
  // Probe on R22_out
  // Probe on R23_out
  // Probe on R24_out
  // Probe on R25_out
  // Probe on R26_out
  // Probe on R27_out
  // Probe on R28_out
  // Probe on R29_out
  // Probe on R30_out
  // Probe on R31_out
  Multiplexer #(.select(5), .width(32), .enable("false")) multiplexer_2 (
    .in0(R0_out), .in1(R1_out), .in2(R2_out), .in3(R3_out), .in4(R4_out), .in5(R5_out), .in6(R6_out),
    .in7(R7_out), .in8(R8_out), .in9(R9_out), .in10(R10_out), .in11(R11_out), .in12(R12_out), .in13(R13_out),
    .in14(R14_out), .in15(R15_out), .in16(R16_out), .in17(R17_out), .in18(R18_out), .in19(R19_out),
    .in20(R20_out), .in21(R21_out), .in22(R22_out), .in23(R23_out), .in24(R24_out), .in25(R25_out),
    .in26(R26_out), .in27(R27_out), .in28(R28_out), .in29(R29_out), .in30(R30_out), .in31(R31_out), .out(RB),
    .sel(ID_Rb));

  // Other names for the same wires on the sheet: clear = clear_registers; clk = clock;
  //   write_en = register_write_enable

  // Notes on the sheet:
  //   Inputs to the Register File
  //   32 REGISTERS ( 0 to 31 )
  //   Outputs from the Register File
  //   Selecting the value of RA
  //   Current values of all 32 Regsiters
  //   Helpful during the testing of the Register File circuit
  //   Updating the value of a selected register
  //   Selecting the value of RB
endmodule

module ALU (
  input  [31:0] Input_1,
  input  [31:0] Input_2,
  input  [1:0] Opeartion_selector,
  output [31:0] Output
);

  wire [31:0] adder_1_out, and_1_out, or_1_out, subtractor_1_out;

  Adder #(.width(32)) adder_1 (.a(Input_1), .b(Input_2), .out(adder_1_out));  // open: cin, cout
  Subtractor #(.width(32)) subtractor_1 (.a(Input_1), .b(Input_2), .out(subtractor_1_out));  // open: bin, bout
  assign and_1_out = Input_1 & Input_2;  // AND_Gate and_1, 32 bits wide
  assign or_1_out = Input_1 | Input_2;  // OR_Gate or_1, 32 bits wide
  Multiplexer #(.select(2), .width(32), .enable("false")) multiplexer_1 (
    .in0(adder_1_out), .in1(subtractor_1_out), .in2(and_1_out), .in3(or_1_out), .out(Output),
    .sel(Opeartion_selector));

  // Other names for the same wires on the sheet: alu_output[31:0] = Output; op_selector[1:0] = Opeartion_selector

  // Notes on the sheet:
  //   Inputs to the ALU
  //   ALU Output
endmodule

module Instrucion_Splitter (
  input  [31:0] Instruction,
  output [3:0] op_code,
  output [4:0] ID_Rc,
  output [4:0] ID_Ra,
  output [4:0] ID_Rb,
  output [31:0] Immediate_Value,
  output First_Bit,
  output [1:0] op_select,
  output Immediate_bit
);

  // Probe on Instruction[31:28]
  // Probe on Instruction[27:23]
  // Probe on Instruction[22:18]
  // Probe on Instruction[17:13]
  // Probe on {{19{1'b0}}, Instruction[12:0]}

  assign First_Bit = Instruction[31];
  assign ID_Ra = Instruction[22:18];
  assign ID_Rb = Instruction[17:13];
  assign ID_Rc = Instruction[27:23];
  assign Immediate_bit = Instruction[28];
  assign Immediate_Value = {{19{1'b0}}, Instruction[12:0]};
  assign op_code = Instruction[31:28];
  assign op_select = Instruction[30:29];

  // Other names for the same wires on the sheet: d18 = Instruction[18]; d19 = Instruction[19]; d20 = Instruction[20];
  //   d21 = Instruction[21]; d22 = Instruction[22]; d13 = Instruction[13]; d14 = Instruction[14];
  //   d15 = Instruction[15]; d16 = Instruction[16]; d17 = Instruction[17]; d23 = Instruction[23];
  //   d24 = Instruction[24]; d25 = Instruction[25]; d26 = Instruction[26]; d27 = Instruction[27]; d0 = Instruction[0];
  //   imdt_val[12:0] = Instruction[12:0]; d1 = Instruction[1]; d2 = Instruction[2]; d3 = Instruction[3];
  //   d4 = Instruction[4]; d5 = Instruction[5]; d6 = Instruction[6]; d7 = Instruction[7]; d8 = Instruction[8];
  //   d9 = Instruction[9]; d10 = Instruction[10]; d11 = Instruction[11]; d12 = Instruction[12]; d28 = Instruction[28];
  //   d29 = Instruction[29]; d30 = Instruction[30]; d31 = Instruction[31]

  // Notes on the sheet:
  //   INPUT
  //   OUTPUTS
endmodule

module control_signals_generator (
  input  Clock,
  input  [3:0] op_code,
  output Stage_1,
  output Stage_2,
  output Stage_3,
  output Stage_4,
  output Stage_5,
  output PC_en,
  output IR_en,
  output S1,
  output S2,
  output HLT,
  output reg_write_enable,
  output S_ALU,
  output Ra_en,
  output Rz_en,
  output mem_en,
  output ALU_en,
  output Rb_en,
  output Ry_en,
  output load
);

  wire and_1_out, and_3_out, and_4_out, and_5_out, and_6_out, and_10_out, and_11_out, and_12_out, and_13_out,
       and_14_out, and_15_out, and_16_out, and_17_out, not_1_out, or_1_out, or_2_out;
  wire [2:0] counter_1_q;

  Counter #(.width(3), .max('h4)) counter_1 (.Q(counter_1_q), .clk(Clock));  // open: load, D, count, carry, clr
  // Probe on counter_1_q
  or or_1 (or_1_out, Ra_en, ALU_en);
  Decoder #(.select(3), .enable("false")) decoder_1 (
    .out0(IR_en), .out1(Ra_en), .out2(ALU_en), .out3(Ry_en), .out4(Stage_5), .sel(counter_1_q));  // open: out5, out6, out7
  and and_1 (and_1_out, Ry_en, ~op_code[0], ~op_code[1], ~op_code[2], ~op_code[3]);  // AND_Gate
  and and_2 (S_ALU, or_1_out, op_code[0], op_code[1], ~op_code[2], ~op_code[3]);  // AND_Gate
  and and_3 (and_3_out, Ry_en, op_code[0], ~op_code[1], ~op_code[2], ~op_code[3]);  // AND_Gate
  and and_4 (and_4_out, ~op_code[0], ~op_code[1], ~op_code[2], ~op_code[3]);  // AND_Gate
  and and_5 (and_5_out, op_code[0], ~op_code[1], ~op_code[2], ~op_code[3]);  // AND_Gate
  not not_1 (not_1_out, and_6_out);
  and and_6 (and_6_out, op_code[0], ~op_code[1], ~op_code[2], ~op_code[3]);  // AND_Gate
  not not_2 (S2, and_1_out);
  not not_3 (load, and_3_out);
  or or_2 (or_2_out, and_4_out, and_5_out);
  and and_7 (reg_write_enable, not_1_out, Stage_5);
  and and_8 (mem_en, or_2_out, Ry_en);
  and and_9 (HLT, ~op_code[0], ~op_code[1], op_code[2], ~op_code[3]);  // AND_Gate
  and and_10 (and_10_out, ALU_en, ~op_code[0], op_code[1], ~op_code[2], ~op_code[3]);  // AND_Gate
  and and_11 (and_11_out, ALU_en, op_code[0], op_code[1], ~op_code[2], ~op_code[3]);  // AND_Gate
  and and_12 (and_12_out, ALU_en, ~op_code[0], ~op_code[1], ~op_code[2], ~op_code[3]);  // AND_Gate
  and and_13 (and_13_out, ALU_en, op_code[0], ~op_code[1], ~op_code[2], ~op_code[3]);  // AND_Gate
  and and_14 (and_14_out, ALU_en, op_code[0], ~op_code[1], ~op_code[2], op_code[3]);  // AND_Gate
  and and_15 (and_15_out, ALU_en, op_code[0], op_code[1], ~op_code[2], op_code[3]);  // AND_Gate
  and and_16 (and_16_out, ALU_en, op_code[0], ~op_code[1], op_code[2], op_code[3]);  // AND_Gate
  and and_17 (and_17_out, ALU_en, op_code[0], op_code[1], op_code[2], op_code[3]);
  or or_3 (S1, and_10_out, and_11_out, and_12_out, and_13_out, and_14_out, and_15_out, and_16_out, and_17_out);

  assign PC_en = IR_en;
  assign Rb_en = Ra_en;
  assign Rz_en = ALU_en;
  assign Stage_1 = IR_en;
  assign Stage_2 = Ra_en;
  assign Stage_3 = ALU_en;
  assign Stage_4 = Ry_en;

  // Other names for the same wires on the sheet: CLK = Clock; d0 = op_code[0]; d1 = op_code[1]; d2 = op_code[2];
  //   d3 = op_code[3]

  // Notes on the sheet:
  //   STORE
  //   LOAD
  //   STORE
  //   STORE
  //   LOAD
  //   MVI
  //   Inputs to Control Signal Generator
  //   Circuit to find the Stage using number of clock cycles
  //   MOV
  //   MVI
  //   LOAD
  //   STORE
  //   ADI
  //   SUI
  //   ANI
  //   ORI
  //   CONTROL SIGNALS
endmodule
